# Fritzing sketch ChauSze_SeniorDesign1_BBTiny1_PCB (saved by Fritzing 0.9.2b)
circuit board: 6.2cm x 4.8cm
breadboards: 1

parts:
  U1 = attiny85 [package=dip]
  J1 = Power plug
  R1 = Resistor [tolerance=±5% resistance=2.2k package="0805 [SMD]"]
  R2 = Resistor [tolerance=±5% resistance=3.3k package="0805 [SMD]"]
  U2 = GA1A1S202WP Analog Light Sensor
  D3 = LED - 5mm [color="Infrared (940nm)" current=100mA package="5 mm [THT]"]
  D2 = LED - 5mm [color="Infrared (940nm)" current=100mA package="5 mm [THT]"]
  R_D1 = Resistor [tolerance=±5% resistance=33 package=THT]
  R_D3 = Resistor [tolerance=±5% resistance=33 package=THT]
  R_D2 = Resistor [tolerance=±5% resistance=33 package=THT]
  D1 = LED - 5mm [color="Infrared (940nm)" current=100mA package="5 mm [THT]"]

nets:
  N1: U1.Pin_2, D2.anode
  N2: U1.Pin_3, D3.anode
  VCC: U1.Pin_4, U1.Pin_5, U1.Pin_8, J1.VCC, R1.Pin_0, R1.Pin_1, R2.Pin_1, U2.VCC
  N3: U1.Pin_6, D1.anode
  N4: U1.Pin_7, U2.OUT
  GND: J1.GND, R2.Pin_0, U2.GND, R_D1.Pin_0, R_D3.Pin_0, R_D2.Pin_0
  N5: D3.cathode, R_D3.Pin_1
  N6: D2.cathode, R_D2.Pin_1
  N7: R_D1.Pin_1, D1.cathode

notes:
  5VDC
  CHAU
  2016
  Night Vision

custom parts:
  GA1A1S202WP Analog Light Sensor: Description: Basic breakout board for the GA1A1S202WP Ambient Light Sensor. Only what you need, nothing you don't. Sensor acts like a transistor - the greater the incoming light, the higher the analog voltage on the signal pin.
