# Fritzing sketch ChauSze_SeniorDesign1_BBTiny2_PCB (saved by Fritzing 0.9.2b)
circuit board: 6.2cm x 4.8cm
breadboards: 1

parts:
  U1 = attiny85 [package=dip]
  J1 = Power plug
  R1 = Resistor [tolerance=±5% resistance=2.2k package="0805 [SMD]"]
  R2 = Resistor [tolerance=±5% resistance=3.3k package="0805 [SMD]"]
  U2 = GA1A1S202WP Analog Light Sensor
  D3a = LED - 5mm [color="Infrared (940nm)" current=100mA package="5 mm [THT]"]
  D2a = LED - 5mm [color="Infrared (940nm)" current=100mA package="5 mm [THT]"]
  R_D1 = Resistor [tolerance=±5% resistance=33 package=THT]
  R_D3 = Resistor [tolerance=±5% resistance=33 package=THT]
  R_D2 = Resistor [tolerance=±5% resistance=33 package=THT]
  D1a = LED - 5mm [color="Infrared (940nm)" current=100mA package="5 mm [THT]"]
  D3b = LED - 5mm [color="Infrared (940nm)" current=100mA package="5 mm [THT]"]
  D2b = LED - 5mm [color="Infrared (940nm)" current=100mA package="5 mm [THT]"]
  D1b = LED - 5mm [color="Infrared (940nm)" current=100mA package="5 mm [THT]"]

nets:
  N1: U1.Pin_2, D2a.anode
  N2: U1.Pin_3, D3a.anode
  VCC: U1.Pin_4, U1.Pin_5, U1.Pin_8, J1.VCC, R1.Pin_0, R1.Pin_1, R2.Pin_1, U2.VCC
  N3: U1.Pin_6, D1a.anode
  N4: U1.Pin_7, U2.OUT
  GND: J1.GND, R2.Pin_0, U2.GND, R_D1.Pin_0, R_D3.Pin_0, R_D2.Pin_0
  N5: D3a.cathode, D3b.anode
  N6: D2a.cathode, D2b.anode
  N7: R_D1.Pin_1, D1b.cathode
  N8: R_D3.Pin_1, D3b.cathode
  N9: R_D2.Pin_1, D2b.cathode
  N10: D1a.cathode, D1b.anode

notes:
  5VDC
  CHAU
  2016
  Night Vision

custom parts:
  GA1A1S202WP Analog Light Sensor: Description: Basic breakout board for the GA1A1S202WP Ambient Light Sensor. Only what you need, nothing you don't. Sensor acts like a transistor - the greater the incoming light, the higher the analog voltage on the signal pin.
