# Fritzing sketch ChauSze_SeniorDesign1_BBTiny2_Schem (saved by Fritzing 0.9.2b)
breadboards: 1

parts:
  U1 = attiny85 [package=dip]
  J1 = Power plug
  R1 = Resistor [tolerance=±5% resistance=1.7k package="0805 [SMD]"]
  R2 = Resistor [tolerance=±5% resistance=3.3k package="0805 [SMD]"]
  U2 = GA1A1S202WP Analog Light Sensor
  D1a = LED - 5mm [color="Infrared (940nm)" current=100mA package="5 mm [THT]"]
  D2a = LED - 5mm [color="Infrared (940nm)" current=100mA package="5 mm [THT]"]
  R_D3 = Resistor [tolerance=±5% resistance=27 package=THT]
  R_D1 = Resistor [tolerance=±5% resistance=27 package=THT]
  R_D2 = Resistor [tolerance=±5% resistance=27 package=THT]
  D3a = LED - 5mm [color="Infrared (940nm)" current=100mA package="5 mm [THT]"]
  D1b = LED - 5mm [color="Infrared (940nm)" current=100mA package="5 mm [THT]"]
  D2b = LED - 5mm [color="Infrared (940nm)" current=100mA package="5 mm [THT]"]
  D3b = LED - 5mm [color="Infrared (940nm)" current=100mA package="5 mm [THT]"]

nets:
  N1: U1.Pin_2, D1a.anode
  N2: U1.Pin_3, D2a.anode
  GND: U1.Pin_4, J1.GND, R2.Pin_0, U2.GND, R_D3.Pin_0, R_D1.Pin_0, R_D2.Pin_0
  N3: U1.Pin_5, R1.Pin_1, R2.Pin_1
  N4: U1.Pin_6, D3a.anode
  N5: U1.Pin_7, U2.OUT
  VCC: U1.Pin_8, J1.VCC, R1.Pin_0, U2.VCC
  N6: D1a.cathode, D1b.anode
  N7: D2a.cathode, D2b.anode
  N8: R_D3.Pin_1, D3b.cathode
  N9: R_D1.Pin_1, D1b.cathode
  N10: R_D2.Pin_1, D2b.cathode
  N11: D3a.cathode, D3b.anode

notes:
  5V
  Home Surveillance System, Night Vision Block Second Iteration: 6 LEDs, 1

custom parts:
  GA1A1S202WP Analog Light Sensor: Description: Basic breakout board for the GA1A1S202WP Ambient Light Sensor. Only what you need, nothing you don't. Sensor acts like a transistor - the greater the incoming light, the higher the analog voltage on the signal pin.
